# Fritzing sketch AVRGait_sch (saved by Fritzing 0.9.3b)

parts:
  3_Axis_Acclero_&_Gyro = InvenSense MPU6050
  ESP32_-_Controller_+_Bluetooth = Adafruit HUZZAH32 ESP32 Feather [part_number="Adafruit #3405"]
  3_7v_Rechargable_Li-Po_Battery = LIPO-1000mAh [package=lipo-1000]
  RGB_Status_LED = RGB LED (com. cathode, rbg) [package="5 mm [THT]"]
  SPST_Switch = SPST Switch [package=switch-spdt_kit]

nets:
  VCC: 3_Axis_Acclero_&_Gyro.VCC, ESP32_-_Controller_+_Bluetooth.3.3V
  GND: 3_Axis_Acclero_&_Gyro.GND, ESP32_-_Controller_+_Bluetooth.GND, 3_7v_Rechargable_Li-Po_Battery.-, RGB_Status_LED.common_cathode
  N1: 3_Axis_Acclero_&_Gyro.SCL, ESP32_-_Controller_+_Bluetooth.SCL
  N2: 3_Axis_Acclero_&_Gyro.SDA, ESP32_-_Controller_+_Bluetooth.SDA
  N3: ESP32_-_Controller_+_Bluetooth.VBAT, SPST_Switch.O
  N4: ESP32_-_Controller_+_Bluetooth.IO12_A11, RGB_Status_LED.red_anode
  N5: ESP32_-_Controller_+_Bluetooth.IO27_A10, RGB_Status_LED.blue_anode
  N6: ESP32_-_Controller_+_Bluetooth.IO32_A7, RGB_Status_LED.green_anode
  N7: 3_7v_Rechargable_Li-Po_Battery.+, SPST_Switch.S

notes:
  MPU6050 - MEMS 3 axis Acclerometer & Gyroscope
  ESP32 - Controller + Bluetooth
  3.7 v Li-Po battery
  RGB Status Indicator LED
  SPST Switch
